# Fritzing sketch ESP32_adxl345_dht11 (saved by Fritzing 0.8.7b)

parts:
  U1 = ESP32-38PinWide [part_number=ESP32-38PinWide]
  Part1 = Adafruit ADXL345 [part_number="Adafruit #1231"]
  DHT1 = DHT11 Humitidy and Temperature Sensor (3 pins)

nets:
  N1: U1.GPIO33, DHT1.DATA
  GND: U1.GND, Part1.GND, DHT1.GND
  VIN: U1.VIN, DHT1.VDD
  N2: U1.GPIO21, Part1.SDA/SDIO
  N3: U1.GPIO22, Part1.SCL

custom parts:
  ESP32-38PinWide: Generic 38-Pin ESP32 with wide format (only access to one side of pins on a breadboard) based on Stephen Lilley's HiLetgo ESP-WROOM-32 ESP32 ESP-32S Development Board.
  Adafruit ADXL345: Filling out our accelerometer offerings, we now have the really lovely digital ADXL345 from Analog Devices, a triple-axis accelerometer with digital I2C and SPI interface breakout. We added an on-board 3.3V regulator and logic-level shifting circuitry, making it a perfect choice for interfacing with any 3V or 5V microcontroller such as the Arduino. The sensor has three axes of measurements, X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
  DHT11 Humitidy and Temperature Sensor (3 pins): DHT11 Humidity and Temperature Sensor (3 pins) from the design created by John De Cristofaro for Adafruit Industries.
